# Fritzing sketch dht11 (saved by Fritzing 0.8.4b)
breadboards: 1

parts:
  元件1 = Arduino Uno (Rev3)
  RHT1 = Humidity and Temperature Sensor RHT03

nets:
  N1: 元件1.GND, RHT1.GND_2
  N2: 元件1.D2, RHT1.Data-signal
  3V3: 元件1.3V3, RHT1.Vcc
