# Fritzing sketch led (saved by Fritzing 0.8.4b)
breadboards: 1

parts:
  元件1 = Arduino Uno (Rev3)
  S1 = Pushbutton [package="[THT]"]
  R1 = Resistor [tolerance=±5% resistance=220 package=THT]
  LED2 = RGB LED (com. anode, rbg) [package="5 mm [THT]"]

nets:
  N1: 元件1.GND, R1.Pin_1, LED2.blue_cathode
  N2: 元件1.D9_PWM, LED2.green_cathode
  N3: 元件1.D10_PWM/SS, LED2.common_anode
  N4: 元件1.D11_PWM/MOSI, LED2.red_cathode
  N5: 元件1.D2, 元件1.3V3, S1.Pin_3, S1.Pin_4
  N6: S1.Pin_1, S1.Pin_2, R1.Pin_0
