# Fritzing sketch servo-motor (saved by Fritzing 0.8.4b)

parts:
  元件1 = Arduino Uno (Rev3)
  M1 = DC Motor
  J1 = Basic Servo

nets:
  GND: 元件1.GND, M1.pin_2, J1.gnd
  N1: 元件1.D9_PWM, J1.pulse
  N2: 元件1.D6_PWM, M1.pin_1
  5V: 元件1.5V, J1.vcc
